# Fritzing sketch AR22_2LED (saved by Fritzing 0.9.3b)
breadboards: 1

parts:
  부품1 = Arduino Uno (Rev3)
  LED1 = LED - 5mm [color="Red (633nm)" package="5 mm [THT]"]
  R1 = Resistor [tolerance=±5% resistance=330 package=THT]
  LED2 = LED - 5mm [color="Green (560nm)" package="5 mm [THT]"]
  R2 = Resistor [tolerance=±5% resistance=330 package=THT]

nets:
  N1: 부품1.D3_PWM, LED2.anode
  N2: 부품1.D5_PWM, LED1.anode
  N3: 부품1.GND, R1.Pin_0, LED2.cathode, R2.Pin_1
