# Fritzing sketch AR22_4LED (saved by Fritzing 0.9.3b)
breadboards: 1

parts:
  부품1 = Arduino Uno (Rev3)
  LED1 = LED - 5mm [color="Red (633nm)" package="5 mm [THT]"]
  R1 = Resistor [tolerance=±5% resistance=330 package=THT]
  LED2 = LED - 5mm [color="Green (560nm)" package="5 mm [THT]"]
  R2 = Resistor [tolerance=±5% resistance=330 package=THT]
  LED3 = LED - 5mm [color="Blue (430nm)" package="5 mm [THT]"]
  R3 = Resistor [tolerance=±5% resistance=330 package=THT]
  LED4 = LED - 5mm [color="Yellow (595nm)" package="5 mm [THT]"]
  R4 = Resistor [tolerance=±5% resistance=330 package=THT]

nets:
  N1: 부품1.D9_PWM, LED4.anode
  N2: 부품1.D3_PWM, LED2.anode
  N3: 부품1.D5_PWM, LED1.anode
  N4: 부품1.D6_PWM, LED3.anode
  N5: 부품1.GND, R1.Pin_0, R2.Pin_0, R3.Pin_0, R4.Pin_0
  N6: LED2.cathode, R2.Pin_1
  N7: LED3.cathode, R3.Pin_1
  N8: LED4.cathode, R4.Pin_1
