# Fritzing sketch 두더지잡기 (saved by Fritzing 0.9.3b)
breadboards: 1

parts:
  부품1 = Arduino Uno (Rev3)
  S1 = Momentary Switch [package=ksa_sealed_tac_switch]
  S2 = Momentary Switch [package=ksa_sealed_tac_switch]
  S3 = Momentary Switch [package=ksa_sealed_tac_switch]
  S4 = Momentary Switch [package=ksa_sealed_tac_switch]
  S6 = Momentary Switch [package=ksa_sealed_tac_switch]
  R2 = Resistor [tolerance=±5% resistance=220 package=THT]
  R3 = Resistor [tolerance=±5% resistance=220 package=THT]
  R4 = Resistor [tolerance=±5% resistance=220 package=THT]
  R5 = Resistor [tolerance=±5% resistance=220 package=THT]
  R6 = Resistor [tolerance=±5% resistance=220 package=THT]
  R7 = Resistor [tolerance=±5% resistance=220 package=THT]
  R8 = Resistor [tolerance=±5% resistance=220 package=THT]
  R9 = Resistor [tolerance=±5% resistance=220 package=THT]
  J1 = Piezo Speaker
  S7 = Momentary Switch [package=ksa_sealed_tac_switch]
  LED13 = LED - 5mm [color="Red (633nm)" package="5 mm [THT]"]
  LED14 = LED - 5mm [color="Red (633nm)" package="5 mm [THT]"]
  LED15 = LED - 5mm [color="Red (633nm)" package="5 mm [THT]"]
  LED16 = LED - 5mm [color="Red (633nm)" package="5 mm [THT]"]
  LED17 = LED - 5mm [color="Red (633nm)" package="5 mm [THT]"]

nets:
  N1: 부품1.A0, S1.1
  N2: 부품1.A1, S2.1
  N3: 부품1.A2, S3.1
  N4: 부품1.A3, S4.1
  N5: 부품1.A4/SDA, S6.1
  N6: 부품1.D8, J1.pin2
  N7: 부품1.D10_PWM/SS, R3.Pin_0
  N8: 부품1.D11_PWM/MOSI, R4.Pin_0
  N9: 부품1.D12/MISO, R5.Pin_0
  N10: 부품1.GND, S1.2, S2.2, S3.2, S4.2, S6.2, J1.pin1, S7.4, LED13.anode, LED14.anode, LED15.anode, LED16.anode, LED17.anode
  N11: 부품1.D0/RX, S7.2
  N12: 부품1.D1/TX, R6.Pin_0
  N13: 부품1.D2, R9.Pin_0
  N14: 부품1.D3_PWM, R7.Pin_0
  N15: 부품1.D4, R8.Pin_0
  N16: 부품1.D5_PWM, R2.Pin_0
  N17: R2.Pin_1, LED17.cathode
  N18: R6.Pin_1, LED13.cathode
  N19: R7.Pin_1, LED15.cathode
  N20: R8.Pin_1, LED16.cathode
  N21: R9.Pin_1, LED14.cathode
